# Fritzing sketch Scheme (saved by Fritzing 0.9.3b)
circuit board: 8.46667cm x 5.64444cm
breadboards: 2

parts:
  Main = Arduino Nano (Rev3.0)
  Reg = 74HC595 [package="DIP16 [THT]"]
  LED1 = 7-SEGMENT-4DIGIT-YOUNGSUN [package=7-segment-4digit-youngsun-longpads]
  S1 = Pushbutton [package="[THT]"]
  S2 = Pushbutton [package="[THT]"]
  OMRON1 = OMRON PCB Power Relay – G5LE [part_number="G5LE-1\n" package=THT]
  C1 = Capacitor [package=cap-pth-small2]

nets:
  GND: Main.GND, Reg.GND, Reg.Q7', Reg.OE, S1.Pin_1, S1.Pin_2, S2.Pin_1, S2.Pin_2, OMRON1.COIL1, C1.1
  N1: Main.D2, Reg.ST_CP, C1.2
  N2: Main.D3, Reg.DS
  N3: Main.D4, Reg.SH_CP
  N4: Main.D5, LED1.G
  N5: Main.D6, LED1.COL-C
  N6: Main.D7, LED1.F
  N7: Main.D8, LED1.DP
  N8: Main.D9, S1.Pin_3, S1.Pin_4
  N9: Main.D10, S2.Pin_3, S2.Pin_4
  N10: Main.D11/MOSI, OMRON1.C
  5V: Main.5V, Reg.MR, Reg.VCC, OMRON1.COIL2
  N11: Reg.Q1, LED1.DIG3
  N12: Reg.Q2, LED1.C
  N13: Reg.Q3, LED1.DIG2
  N14: Reg.Q4, LED1.D
  N15: Reg.Q5, LED1.E
  N16: Reg.Q6, LED1.APOS-A
  N17: Reg.Q7, LED1.A
  N18: Reg.Q0, LED1.COL-A
